# Fritzing sketch Puente-Fritzing (saved by Fritzing 0.9.3b)
perfboards: 1

parts:
  IC1 = H-Bridge [package=THT]
  J1 = Screw terminal - 2 pins [package=THT]
  J6 = Screw terminal - 2 pins [package=THT]
  U4 = SWITCH-SPST-2 [package=switch-spst-vertical]
  R1 = Resistor [tolerance=±10% resistance=330 package=THT]
  R2 = Resistor [tolerance=±10% resistance=330 package=THT]
  LED1 = LED - 5mm [color="Red (633nm)" package="5 mm [THT]"]
  LED2 = LED - 5mm [color="Green (565nm)" package="5 mm [THT]"]
  Componente1 = Arduino Uno (Rev3)
  Componente4 = Bluetooth HC-05 Hembra
  M1 = Hobby Gearmotor with 48:1 gearbox [part_number=ROB-13302]  # not connected
  LED3 = LED - 5mm [color="Yellow (585nm)" package="5 mm [THT]"]
  R3 = Resistor [tolerance=±10% resistance=330 package=THT]

nets:
  N1: IC1.1_2EN, IC1.VCC1
  N2: IC1.1A, Componente1.D6_PWM
  GND2: IC1.GND2, J1.pin2, Componente1.GND
  N3: IC1.2A, Componente1.D5_PWM
  5V: J1.pin1, Componente1.5V, Componente4.VCC
  N4: J6.pin2, U4.P
  N5: U4.O, Componente1.VIN
  N6: R1.Pin_0, LED1.cathode
  N7: R2.Pin_0, LED2.cathode
  N8: LED1.anode, Componente1.D4
  N9: LED2.anode, Componente1.D2
  N10: Componente1.D0/RX, Componente4.TXD
  N11: Componente1.D1/TX, Componente4.RXD
  N12: Componente1.D3_PWM, LED3.anode
  N13: LED3.cathode, R3.Pin_0
